// Logisim project TFC_ERS_3864K.circ as structural Verilog
module main (
);

  wire and_1_out, and_2_out, and_3_out, and_4_out, clock_1_out, comparator_1_eq, cpu_1_cpu_daten_aktiv,
       cpu_1_cpu_out_daisychains00, cpu_1_cpu_out_intmaskiert, cpu_1_cpu_out_weiter,
       cpu_1_cpu_out_weiterzwei, d_ff_1_q, keyboard_1_avail, mod4_speicher_1_mod4_out_daisychain,
       mod4_speicher_1_mod4_out_svwert, mod4_speicher_1_mod4_ram_lade, mod4_speicher_1_mod4_ram_speicher,
       not_1_out, or_1_out, or_2_out, or_3_out;
  wire [6:0] controlled_buffer_1_out, keyboard_1_data;
  wire [7:0] bit_extender_2_out, cpu_1_cpu_bus_adr, mod4_speicher_1_mod4_out_icnummer, or_5_out,
       pull_resistor_2_node, pull_resistor_3_node;
  wire [15:0] bit_extender_1_out, cpu_1_cpu_bus_daten, mod4_speicher_1_mod4_out_wert,
       mod4_speicher_1_mod4_ram_daten, or_4_out, ram_1_dout, rom_1_data;
  wire [23:0] cpu_1_cpu_rom_adresse, mod4_speicher_1_mod4_ram_adr;

  Clock clock_1 (.out(clock_1_out));
  ROM #(.addrWidth(24), .dataWidth(16)) rom_1 (.addr(cpu_1_cpu_rom_adresse), .data(rom_1_data));
  D_Flip_Flop d_ff_1 (.Q(d_ff_1_q), .preset(and_2_out), .reset(not_1_out));  // open: D, clk, Qn
  not not_1 (not_1_out, cpu_1_cpu_out_intmaskiert);
  Keyboard #(.trigger("falling")) keyboard_1 (
    .clk(clock_1_out), .re(and_1_out), .avail(keyboard_1_avail), .data(keyboard_1_data));  // open: clr
  and and_1 (and_1_out, cpu_1_cpu_out_intmaskiert, cpu_1_cpu_out_weiterzwei);
  CPU cpu_1 (
    .Takt(clock_1_out), .ROM_CU_Befehle(rom_1_data), .Mod_IC_IntNummer(or_5_out), .Mod_IC_IntWert(or_4_out),
    .Mod_IC_DaisychainH0F(mod4_speicher_1_mod4_out_daisychain), .Mod_Intern_KurzerWert(or_2_out),
    .CPU_Bus_Adr(cpu_1_cpu_bus_adr), .CPU_Out_Weiter(cpu_1_cpu_out_weiter),
    .CPU_Out_WeiterZwei(cpu_1_cpu_out_weiterzwei), .CPU_Bus_Daten(cpu_1_cpu_bus_daten),
    .CPU_Daten_Aktiv(cpu_1_cpu_daten_aktiv), .CPU_Out_DaisychainS00(cpu_1_cpu_out_daisychains00),
    .CPU_ROM_Adresse(cpu_1_cpu_rom_adresse), .CPU_Out_IntMaskiert(cpu_1_cpu_out_intmaskiert));
  assign controlled_buffer_1_out = or_1_out ? keyboard_1_data : 7'bz;  // Controlled_Buffer controlled_buffer_1
  Pull_Resistor pull_resistor_1 (.node(controlled_buffer_1_out));
  Pull_Resistor pull_resistor_2 (.node(pull_resistor_2_node));
  assign pull_resistor_2_node = or_1_out ? pull_resistor_3_node : 8'bz;  // Controlled_Buffer controlled_buffer_2
  Pull_Resistor pull_resistor_3 (.node(pull_resistor_3_node));
  or or_1 (or_1_out, d_ff_1_q, and_2_out);
  and and_2 (and_2_out, ~cpu_1_cpu_out_daisychains00, cpu_1_cpu_out_weiterzwei, keyboard_1_avail);  // AND_Gate
  or or_2 (or_2_out, and_3_out, mod4_speicher_1_mod4_out_svwert);
  assign bit_extender_1_out = {{9{1'b0}}, controlled_buffer_1_out};  // Bit_Extender bit_extender_1
  or or_3 (or_3_out, cpu_1_cpu_out_daisychains00, d_ff_1_q);
  and and_3 (and_3_out, cpu_1_cpu_out_intmaskiert, and_2_out);
  assign or_4_out = bit_extender_1_out | mod4_speicher_1_mod4_out_wert;  // OR_Gate or_4, 16 bits wide
  assign or_5_out = pull_resistor_2_node | mod4_speicher_1_mod4_out_icnummer;  // OR_Gate or_5, 8 bits wide
  TTY #(.rows(24), .cols(64)) tty_1 (
    .data(bit_extender_2_out[6:0]), .clk(clock_1_out), .we(and_4_out), .clr(bit_extender_2_out[7]));
  Bit_Extender #(.in_width(16), .out_width(8), .\type ("zero")) bit_extender_2 (
    .in(cpu_1_cpu_bus_daten), .out(bit_extender_2_out));
  Comparator #(.mode("unsigned")) comparator_1 (.a(8'h2), .b(cpu_1_cpu_bus_adr), .eq(comparator_1_eq));  // open: gt, lt
  and and_4 (and_4_out, comparator_1_eq, cpu_1_cpu_out_weiter, cpu_1_cpu_daten_aktiv);
  RAM #(.addrWidth(24), .dataWidth(16), .databus("bibus")) ram_1 (
    .addr(mod4_speicher_1_mod4_ram_adr), .we(mod4_speicher_1_mod4_ram_speicher),
    .oe(mod4_speicher_1_mod4_ram_lade), .clk(clock_1_out), .din(mod4_speicher_1_mod4_ram_daten),
    .dout(ram_1_dout));
  Mod4_Speicher mod4_speicher_1 (
    .CPU_Mod4_Adresse(cpu_1_cpu_bus_adr), .CPU_Mod4_Weiter(cpu_1_cpu_out_weiter),
    .CPU_Mod4_WeiterZwei(cpu_1_cpu_out_weiterzwei), .CPU_Mod4_Daten(cpu_1_cpu_bus_daten),
    .CPU_Mod4_Sende(cpu_1_cpu_daten_aktiv), .Mod_Mod4_Daisychain(or_3_out),
    .CPU_Mod4_IntMaskiert(cpu_1_cpu_out_intmaskiert), .Takt(clock_1_out), .RAM_Mod4_Daten(ram_1_dout),
    .Mod4_Out_SvWert(mod4_speicher_1_mod4_out_svwert), .Mod4_Out_Wert(mod4_speicher_1_mod4_out_wert),
    .Mod4_Out_ICNummer(mod4_speicher_1_mod4_out_icnummer),
    .Mod4_Out_Daisychain(mod4_speicher_1_mod4_out_daisychain), .Mod4_RAM_Adr(mod4_speicher_1_mod4_ram_adr),
    .Mod4_RAM_Daten(mod4_speicher_1_mod4_ram_daten), .Mod4_RAM_Speicher(mod4_speicher_1_mod4_ram_speicher),
    .Mod4_RAM_Lade(mod4_speicher_1_mod4_ram_lade));

  // Notes on the sheet:
  //   contents of rom_1 (hex, n*v repeats v):
  //   4000 1010 5000 1000 101d 5000 100d 4000 207c 100d 6003 101d 6004 1011 2062 3500 2031 2042 119c 100d
  //   9400 3100 11ac 100d 9000 3b00 2034 2003 1000 207c 100d 5030 101d 5040 1006 100c 101d 9010 2071 3300
  //   2007 2071 2082 3500 108c 100d 9400 9800 1007 100c 102d 9000 204*0 2071 2082 3500 10dc 101d 9400 1016
  //   2071 3307 108c 100d 9000 2081 3308 2071 3307 207c 100d 1000 5000 101d 5000 1016 108c 100d 9000 230*0
  //   100c 100d e800 1007 2071 207c 100d 6003 102d 5030 3307 2082 2071 3500 115c 102d 9200 2017 104c 102d
  //   9000 1007 108c 100d 9000
endmodule

module CPU (
  input  Takt,
  input  [15:0] ROM_CU_Befehle,
  input  [7:0] Mod_IC_IntNummer,
  input  [15:0] Mod_IC_IntWert,
  input  Mod_IC_DaisychainH0F,
  input  Mod_Intern_KurzerWert,
  output [7:0] CPU_Bus_Adr,
  output CPU_Out_Weiter,
  output CPU_Out_WeiterZwei,
  output [15:0] CPU_Bus_Daten,
  output CPU_Daten_Aktiv,
  output CPU_Out_DaisychainS00,
  output [23:0] CPU_ROM_Adresse,
  output CPU_Out_IntMaskiert
);

  wire and_1_out, and_2_out, and_3_out, and_4_out, and_5_out, and_6_out, cpu_cu_1_cu_counter_branch,
       cpu_cu_1_cu_counter_intcall, cpu_cu_1_cu_ic_modeverletzung, cpu_cu_1_cu_ic_setzteint,
       cpu_cu_1_cu_mmu_setzetlb, cpu_cu_1_cu_out_ladespreg, cpu_cu_1_cu_out_speicherspreg,
       cpu_cu_1_cu_ram_lade, cpu_cu_1_cu_ram_speicher, cpu_cu_1_cu_reg_aluop, cpu_ic_1_ic_out_daisychain1b,
       cpu_ic_1_ic_out_interrupt, cpu_register_1_reg_out_ladestatus, or_2_out;
  wire [3:0] cpu_cu_1_cu_alu_operation, cpu_cu_1_cu_ext_moduladresse, cpu_cu_1_cu_mmu_tlbwahl,
       cpu_cu_1_cu_out_sonderargument, cpu_cu_1_cu_out_sonderregister, cpu_cu_1_cu_out_zusatzargument,
       pull_resistor_3_node;
  wire [7:0] cpu_alu_1_alu_reg_c, cpu_alu_1_alu_reg_status, cpu_cu_1_cu_counter_statusvergleich,
       cpu_cu_1_cu_out_modus, cpu_cu_1_cu_reg_steuerung, cpu_cu_1_cu_reg_wert, cpu_cu_1_cu_reg_zieladresse,
       cpu_ram_1_ram_reg_daten, cpu_register_1_reg_alu_a, cpu_register_1_reg_alu_b,
       cpu_register_1_reg_counter_status, cpu_register_1_reg_out_daten, multiplexer_1_out, or_1_out,
       pull_resistor_1_node, pull_resistor_4_node;
  wire [11:0] rom_1_data;
  wire [15:0] bit_extender_1_out, controlled_buffer_2_out, cpu_counter_1_counter_mmu_adresse,
       cpu_counter_1_counter_reg_adressepe, cpu_cu_1_cu_out_cpumodus, cpu_ic_1_ic_counter_ptr,
       cpu_ic_1_ic_reg_spreg, cpu_register_1_reg_counter_intcalladr, cpu_register_1_reg_out_pointer,
       multiplexer_2_out, or_3_out, register_1_q;
  wire [23:0] cpu_mmu_1_mmu_ram_adresse;

  Pull_Resistor pull_resistor_1 (.node(pull_resistor_1_node));
  assign pull_resistor_1_node = and_1_out ? 8'h10 : 8'bz;  // Controlled_Buffer controlled_buffer_1
  and and_1 (and_1_out, ~Mod_IC_DaisychainH0F, cpu_cu_1_cu_ic_modeverletzung);  // AND_Gate
  assign or_1_out = Mod_IC_IntNummer | pull_resistor_1_node;  // OR_Gate or_1, 8 bits wide
  or or_2 (or_2_out, and_1_out, Mod_IC_DaisychainH0F);
  Register #(.width(16), .trigger("falling")) register_1 (
    .D(Mod_IC_IntWert), .en(Mod_Intern_KurzerWert), .clk(Takt), .Q(register_1_q), .clr(and_2_out));
  and and_2 (and_2_out, CPU_Out_Weiter, and_3_out);
  assign controlled_buffer_2_out = and_3_out ? register_1_q : 16'bz;  // Controlled_Buffer controlled_buffer_2
  Pull_Resistor pull_resistor_2 (.node(controlled_buffer_2_out));
  and and_3 (and_3_out, cpu_cu_1_cu_out_sonderregister[2], cpu_cu_1_cu_out_ladespreg);
  CPU_CU cpu_cu_1 (
    .ROM_CU_Befehle(ROM_CU_Befehle), .Takt(Takt), .Reg_CU_Ptr(cpu_register_1_reg_out_pointer),
    .IC_CU_Int(cpu_ic_1_ic_out_interrupt), .CU_Reg_Steuerung(cpu_cu_1_cu_reg_steuerung),
    .CU_Reg_ALUOP(cpu_cu_1_cu_reg_aluop), .CU_Counter_Branch(cpu_cu_1_cu_counter_branch),
    .CU_RAM_Speicher(cpu_cu_1_cu_ram_speicher), .CU_RAM_Lade(cpu_cu_1_cu_ram_lade),
    .CU_Out_Sende(CPU_Daten_Aktiv), .CU_MMU_SetzeTLB(cpu_cu_1_cu_mmu_setzetlb),
    .CU_IC_SetzteInt(cpu_cu_1_cu_ic_setzteint), .CU_IC_Interrupt(CPU_Out_DaisychainS00),
    .CU_Out_SpeicherSpReg(cpu_cu_1_cu_out_speicherspreg), .CU_Out_LadeSpReg(cpu_cu_1_cu_out_ladespreg),
    .CU_Counter_IntCall(cpu_cu_1_cu_counter_intcall), .CU_Out_Sonderargument(cpu_cu_1_cu_out_sonderargument),
    .CU_Ext_Moduladresse(cpu_cu_1_cu_ext_moduladresse),
    .CU_Out_Sonderregister(cpu_cu_1_cu_out_sonderregister), .CU_MMU_TLBWahl(cpu_cu_1_cu_mmu_tlbwahl),
    .CU_Counter_StatusVergleich(cpu_cu_1_cu_counter_statusvergleich),
    .CU_ALU_Operation(cpu_cu_1_cu_alu_operation), .CU_Out_Modus(cpu_cu_1_cu_out_modus),
    .CU_Reg_Wert(cpu_cu_1_cu_reg_wert), .CU_Reg_Quelladresse(cpu_cu_1_cu_reg_zieladresse[7:4]),
    .CU_Out_Zusatzargument(cpu_cu_1_cu_out_zusatzargument),
    .CU_Reg_Zieladresse(cpu_cu_1_cu_reg_zieladresse[3:0]), .CU_Out_Weiter(CPU_Out_Weiter),
    .CU_Out_WeiterZwei(CPU_Out_WeiterZwei), .CU_IC_ModeVerletzung(cpu_cu_1_cu_ic_modeverletzung),
    .CU_Out_CPUModus({cpu_cu_1_cu_out_cpumodus[15:4], CPU_Out_IntMaskiert, cpu_cu_1_cu_out_cpumodus[2:0]}));  // open: Int_CU_ROMZugriff, Int_CU_RAMZugriff
  ROM #(.addrWidth(4), .dataWidth(12)) rom_1 (.addr(pull_resistor_3_node), .data(rom_1_data));
  Pull_Resistor pull_resistor_3 (.node(pull_resistor_3_node));
  assign pull_resistor_3_node = CPU_Out_Weiter ? cpu_cu_1_cu_alu_operation : 4'bz;  // Controlled_Buffer controlled_buffer_3
  and and_4 (and_4_out, CPU_Out_Weiter, cpu_cu_1_cu_out_sonderargument[1]);
  Multiplexer #(.width(8), .enable("false")) multiplexer_1 (
    .in0(cpu_register_1_reg_out_daten), .in1(or_1_out), .out(multiplexer_1_out), .sel(and_5_out));
  and and_5 (and_5_out, ~CPU_Out_DaisychainS00, cpu_ic_1_ic_out_interrupt);  // AND_Gate
  CPU_ALU cpu_alu_1 (
    .CU_ALU_Arg(rom_1_data), .Reg_ALU_A(cpu_register_1_reg_alu_a), .Reg_ALU_B(cpu_register_1_reg_alu_b),
    .ALU_Reg_Status(cpu_alu_1_alu_reg_status), .ALU_Reg_C(cpu_alu_1_alu_reg_c));
  CPU_RAM cpu_ram_1 (
    .Reg_RAM_Pointer(cpu_mmu_1_mmu_ram_adresse), .CU_RAM_Speicher(cpu_cu_1_cu_ram_speicher),
    .CU_RAM_Lade(cpu_cu_1_cu_ram_lade), .Takt(Takt), .CU_RAM_Weiter(CPU_Out_Weiter),
    .Reg_RAM_Daten(cpu_register_1_reg_out_daten), .RAM_Reg_Daten(cpu_ram_1_ram_reg_daten));
  CPU_Counter cpu_counter_1 (
    .Reg_Counter_Pointer(cpu_register_1_reg_out_pointer),
    .Reg_Counter_IntCall(cpu_register_1_reg_counter_intcalladr), .IC_Counter_IntPtr(cpu_ic_1_ic_counter_ptr),
    .Takt(Takt), .CU_Counter_Weiter(CPU_Out_WeiterZwei), .CU_Counter_Branch(cpu_cu_1_cu_counter_branch),
    .CU_Counter_IntCallPtr(cpu_cu_1_cu_counter_intcall), .IC_Counter_Int(cpu_ic_1_ic_out_interrupt),
    .Reg_Counter_Status(cpu_register_1_reg_counter_status),
    .CU_Counter_Status(cpu_cu_1_cu_counter_statusvergleich), .Out_Counter_Reset(and_4_out),
    .Counter_Reg_AdressePE(cpu_counter_1_counter_reg_adressepe),
    .Counter_MMU_Adresse(cpu_counter_1_counter_mmu_adresse));
  CPU_IC cpu_ic_1 (
    .Out_IC_IntNummer(multiplexer_1_out), .Reg_IC_IntSaveNummer(cpu_register_1_reg_out_daten),
    .Reg_IC_Pointer(cpu_register_1_reg_out_pointer), .CU_IC_DaisychainEnde(cpu_ic_1_ic_out_daisychain1b),
    .CU_IC_SetzteInt(cpu_cu_1_cu_ic_setzteint), .Takt(Takt), .CU_IC_TimerWeiterZwei(CPU_Out_WeiterZwei),
    .CU_IC_SetzteSonderReg(cpu_cu_1_cu_out_speicherspreg), .CU_IC_LadeSonderReg(cpu_cu_1_cu_out_ladespreg),
    .Out_IC_Daisychain1A(or_2_out),
    .CU_IC_Modus({cpu_cu_1_cu_out_cpumodus[15:4], CPU_Out_IntMaskiert, cpu_cu_1_cu_out_cpumodus[2:0]}),
    .CU_IC_SonderReg(cpu_cu_1_cu_out_sonderregister), .IC_Counter_Ptr(cpu_ic_1_ic_counter_ptr),
    .IC_Out_Daisychain1B(cpu_ic_1_ic_out_daisychain1b), .IC_Reg_SpReg(cpu_ic_1_ic_reg_spreg),
    .IC_Out_Interrupt(cpu_ic_1_ic_out_interrupt));  // open: IC_Out_IntMaskiert
  CPU_MMU cpu_mmu_1 (
    .Counter_MMU_Adresse(cpu_counter_1_counter_mmu_adresse),
    .CU_MMU_Modus({cpu_cu_1_cu_out_cpumodus[15:4], CPU_Out_IntMaskiert, cpu_cu_1_cu_out_cpumodus[2:0]}),
    .CU_MMU_Schreibe(cpu_cu_1_cu_mmu_setzetlb), .Takt(Takt), .CU_MMU_Lesen(CPU_Out_Weiter),
    .CU_MMU_TLBAuswahl(cpu_cu_1_cu_mmu_tlbwahl), .Reg_MMU_TLBAdresse(cpu_register_1_reg_out_daten),
    .Reg_MMU_Pointer(cpu_register_1_reg_out_pointer), .Reg_MMU_RAMAdresse(cpu_register_1_reg_out_pointer),
    .CU_MMU_SchreibeZeit(CPU_Out_WeiterZwei), .MMU_ROM_Adresse(CPU_ROM_Adresse),
    .MMU_RAM_Adresse(cpu_mmu_1_mmu_ram_adresse));
  CPU_Register cpu_register_1 (
    .CU_Reg_Steuerung(cpu_cu_1_cu_reg_steuerung), .CU_Reg_RegAdressen(cpu_cu_1_cu_reg_zieladresse),
    .Out_Reg_Wert(cpu_ram_1_ram_reg_daten), .CU_Reg_Wert(cpu_cu_1_cu_reg_wert),
    .ALU_Reg_C(cpu_alu_1_alu_reg_c), .Out_Reg_Adresse(multiplexer_2_out),
    .CU_Reg_ALUOP(cpu_cu_1_cu_reg_aluop), .Takt(Takt), .ALU_Reg_Status(cpu_alu_1_alu_reg_status),
    .CU_Reg_WeiterZwei(CPU_Out_WeiterZwei), .CU_Reg_Weiter(CPU_Out_Weiter),
    .IC_Reg_Interrupt(cpu_ic_1_ic_out_interrupt),
    .CU_Reg_Modus({cpu_cu_1_cu_out_cpumodus[15:4], CPU_Out_IntMaskiert, cpu_cu_1_cu_out_cpumodus[2:0]}),
    .CU_Reg_SetzteSonderReg(cpu_cu_1_cu_out_speicherspreg), .CU_Reg_LadeSonderReg(cpu_cu_1_cu_out_ladespreg),
    .CU_Reg_SonderReg(cpu_cu_1_cu_out_sonderregister), .Reg_Out_Daten(cpu_register_1_reg_out_daten),
    .Reg_Out_Pointer(cpu_register_1_reg_out_pointer),
    .Reg_Counter_IntCallAdr(cpu_register_1_reg_counter_intcalladr),
    .Reg_Counter_Status(cpu_register_1_reg_counter_status), .Reg_ALU_A(cpu_register_1_reg_alu_a),
    .Reg_ALU_B(cpu_register_1_reg_alu_b), .Reg_Out_LadeStatus(cpu_register_1_reg_out_ladestatus));  // open: Reg_IC_KernelReg
  and and_6 (and_6_out, ~cpu_cu_1_cu_ic_modeverletzung, cpu_cu_1_cu_out_ladespreg);  // AND_Gate
  Pull_Resistor pull_resistor_4 (.node(pull_resistor_4_node));
  assign pull_resistor_4_node = cpu_register_1_reg_out_ladestatus ? cpu_register_1_reg_counter_status : 8'bz;  // Controlled_Buffer controlled_buffer_4
  Multiplexer #(.width(16), .enable("false")) multiplexer_2 (
    .in0(cpu_counter_1_counter_reg_adressepe), .in1(or_3_out), .out(multiplexer_2_out), .sel(and_6_out));
  assign or_3_out = cpu_ic_1_ic_reg_spreg | {cpu_cu_1_cu_out_cpumodus[15:4], CPU_Out_IntMaskiert, cpu_cu_1_cu_out_cpumodus[2:0]} | controlled_buffer_2_out | bit_extender_1_out;  // OR_Gate or_3, 16 bits wide
  assign bit_extender_1_out = {{8{1'b0}}, pull_resistor_4_node};  // Bit_Extender bit_extender_1
  Pull_Resistor pull_resistor_5 (.node(CPU_Bus_Adr));
  assign CPU_Bus_Adr = CPU_Daten_Aktiv ? cpu_register_1_reg_out_daten : 8'bz;  // Controlled_Buffer controlled_buffer_5
  assign CPU_Bus_Daten = CPU_Daten_Aktiv ? cpu_register_1_reg_out_pointer : 16'bz;  // Controlled_Buffer controlled_buffer_6
  Pull_Resistor pull_resistor_6 (.node(CPU_Bus_Daten));

  // Notes on the sheet:
  //   contents of rom_1 (hex, n*v repeats v):
  //   0 3 4b 41 9 18b 45 5 3f 33 27 43 81 101 281 301
endmodule

module CPU_ALU (
  input  [11:0] CU_ALU_Arg,
  input  [7:0] Reg_ALU_A,
  input  [7:0] Reg_ALU_B,
  output [7:0] ALU_Reg_Status,
  output [7:0] ALU_Reg_C
);

  wire and_4_out, and_5_out, and_6_out, and_7_out, and_8_out, and_9_out, and_10_out, and_11_out, and_12_out,
       and_13_out, and_14_out, and_15_out, and_16_out, and_17_out, and_18_out, and_19_out, and_20_out,
       and_21_out, and_22_out, and_23_out, and_24_out, and_25_out, and_26_out, and_27_out, and_28_out,
       and_29_out, and_30_out, and_31_out, and_32_out, and_33_out, and_34_out, and_35_out, and_36_out,
       and_37_out, and_38_out, and_39_out, and_40_out, and_41_out, and_42_out, and_43_out, and_44_out,
       and_45_out, and_46_out, and_47_out, demultiplexer_1_out1, demultiplexer_2_out1, demultiplexer_3_out0,
       demultiplexer_3_out1, demultiplexer_3_out2, demultiplexer_3_out3, demultiplexer_4_out0,
       demultiplexer_4_out1, demultiplexer_4_out2, demultiplexer_4_out3, demultiplexer_5_out0,
       demultiplexer_5_out1, demultiplexer_5_out2, demultiplexer_5_out3, demultiplexer_6_out0,
       demultiplexer_6_out1, demultiplexer_6_out2, demultiplexer_6_out3, demultiplexer_7_out0,
       demultiplexer_7_out1, demultiplexer_7_out2, demultiplexer_7_out3, demultiplexer_8_out0,
       demultiplexer_8_out1, demultiplexer_8_out2, demultiplexer_8_out3, demultiplexer_9_out0,
       demultiplexer_9_out1, demultiplexer_9_out2, demultiplexer_9_out3, demultiplexer_10_out0,
       demultiplexer_10_out1, demultiplexer_10_out2, demultiplexer_10_out3, or_4_out, or_5_out, or_7_out,
       or_8_out, or_10_out, or_11_out, or_14_out, or_16_out, or_17_out, or_19_out, or_20_out, or_22_out,
       or_23_out, or_25_out, or_26_out, xor_1_out, xor_2_out, xor_3_out, xor_4_out, xor_5_out, xor_6_out,
       xor_7_out, xor_8_out, xor_9_out, xor_10_out, xor_11_out, xor_12_out, xor_13_out, xor_14_out,
       xor_15_out, xor_16_out, xor_17_out, xor_18_out, xor_19_out, xor_20_out, xor_21_out, xor_22_out,
       xor_23_out, xor_24_out, xor_25_out, xor_26_out, xor_27_out, xor_28_out, xor_29_out, xor_30_out,
       xor_31_out, xor_32_out;
  wire [9:0] bit_extender_1_out;

  Bit_Extender #(.in_width(12), .out_width(10), .\type ("zero")) bit_extender_1 (
    .in(CU_ALU_Arg), .out(bit_extender_1_out));
  and and_1 (ALU_Reg_Status[7], and_4_out, ~ALU_Reg_Status[0], ~and_5_out);  // AND_Gate
  and and_2 (ALU_Reg_Status[5], and_4_out, ALU_Reg_Status[0], ~and_5_out);  // AND_Gate
  and and_3 (ALU_Reg_Status[6], and_4_out, ~ALU_Reg_Status[0], and_5_out);  // AND_Gate
  and and_4 (and_4_out, bit_extender_1_out[8], bit_extender_1_out[7], bit_extender_1_out[3]);
  or or_1 (ALU_Reg_Status[1], and_6_out, and_7_out);
  Demultiplexer #(.enable("false")) demultiplexer_1 (
    .out0(ALU_Reg_Status[3]), .out1(demultiplexer_1_out1), .in(demultiplexer_3_out1),
    .sel(bit_extender_1_out[9]));
  and and_5 (and_5_out, demultiplexer_10_out3, demultiplexer_9_out3, demultiplexer_8_out3, demultiplexer_7_out3, demultiplexer_6_out3, demultiplexer_5_out3, demultiplexer_4_out3, demultiplexer_3_out3);
  and and_6 (and_6_out, ~xor_2_out, xor_1_out, xor_4_out);  // AND_Gate
  and and_7 (and_7_out, xor_2_out, ~xor_1_out, ~xor_4_out);  // AND_Gate
  Demultiplexer #(.enable("false")) demultiplexer_2 (
    .out0(ALU_Reg_Status[4]), .out1(demultiplexer_2_out1), .in(demultiplexer_10_out2),
    .sel(bit_extender_1_out[9]));
  and and_8 (and_8_out, or_4_out, or_5_out);
  or or_2 (ALU_Reg_Status[0], and_9_out, and_8_out, bit_extender_1_out[5]);
  and and_9 (and_9_out, xor_1_out, xor_4_out);
  xor xor_1 (xor_1_out, and_10_out, bit_extender_1_out[3]);
  and and_10 (and_10_out, Reg_ALU_B[7], bit_extender_1_out[1]);
  or or_3 (ALU_Reg_C[7], demultiplexer_3_out0, demultiplexer_4_out1, demultiplexer_2_out1);
  Demultiplexer #(.select(2), .enable("false")) demultiplexer_3 (
    .out0(demultiplexer_3_out0), .out1(demultiplexer_3_out1), .out2(demultiplexer_3_out2),
    .out3(demultiplexer_3_out3), .in(xor_2_out), .sel(bit_extender_1_out[8:7]));
  xor xor_2 (xor_2_out, or_5_out, or_4_out);
  and and_11 (and_11_out, or_7_out, or_8_out);
  or or_4 (or_4_out, and_13_out, and_11_out, bit_extender_1_out[5]);
  or or_5 (or_5_out, and_12_out, xor_3_out);
  and and_12 (and_12_out, xor_4_out, bit_extender_1_out[4], xor_1_out);
  xor xor_3 (xor_3_out, xor_1_out, xor_4_out);
  and and_13 (and_13_out, xor_8_out, xor_7_out);
  xor xor_4 (xor_4_out, and_14_out, bit_extender_1_out[2]);
  and and_14 (and_14_out, Reg_ALU_A[7], bit_extender_1_out[0]);
  and and_15 (and_15_out, Reg_ALU_B[6], bit_extender_1_out[1]);
  or or_6 (ALU_Reg_C[6], demultiplexer_4_out0, demultiplexer_5_out1, demultiplexer_3_out2);
  Demultiplexer #(.select(2), .enable("false")) demultiplexer_4 (
    .out0(demultiplexer_4_out0), .out1(demultiplexer_4_out1), .out2(demultiplexer_4_out2),
    .out3(demultiplexer_4_out3), .in(xor_5_out), .sel(bit_extender_1_out[8:7]));
  xor xor_5 (xor_5_out, or_8_out, or_7_out);
  and and_16 (and_16_out, or_10_out, or_11_out);
  or or_7 (or_7_out, and_18_out, and_16_out, bit_extender_1_out[5]);
  or or_8 (or_8_out, and_17_out, xor_6_out);
  and and_17 (and_17_out, xor_7_out, bit_extender_1_out[4], xor_8_out);
  xor xor_6 (xor_6_out, xor_8_out, xor_7_out);
  and and_18 (and_18_out, xor_12_out, xor_11_out);
  xor xor_7 (xor_7_out, and_19_out, bit_extender_1_out[2]);
  xor xor_8 (xor_8_out, and_15_out, bit_extender_1_out[3]);
  and and_19 (and_19_out, Reg_ALU_A[6], bit_extender_1_out[0]);
  or or_9 (ALU_Reg_C[5], demultiplexer_5_out0, demultiplexer_6_out1, demultiplexer_4_out2);
  Demultiplexer #(.select(2), .enable("false")) demultiplexer_5 (
    .out0(demultiplexer_5_out0), .out1(demultiplexer_5_out1), .out2(demultiplexer_5_out2),
    .out3(demultiplexer_5_out3), .in(xor_9_out), .sel(bit_extender_1_out[8:7]));
  xor xor_9 (xor_9_out, or_11_out, or_10_out);
  or or_10 (or_10_out, and_25_out, and_23_out, bit_extender_1_out[5]);
  or or_11 (or_11_out, and_20_out, xor_10_out);
  and and_20 (and_20_out, xor_11_out, bit_extender_1_out[4], xor_12_out);
  xor xor_10 (xor_10_out, xor_12_out, xor_11_out);
  xor xor_11 (xor_11_out, and_22_out, bit_extender_1_out[2]);
  xor xor_12 (xor_12_out, and_21_out, bit_extender_1_out[3]);
  and and_21 (and_21_out, Reg_ALU_B[5], bit_extender_1_out[1]);
  and and_22 (and_22_out, Reg_ALU_A[5], bit_extender_1_out[0]);
  or or_12 (ALU_Reg_C[4], demultiplexer_6_out0, demultiplexer_7_out1, demultiplexer_5_out2);
  Demultiplexer #(.select(2), .enable("false")) demultiplexer_6 (
    .out0(demultiplexer_6_out0), .out1(demultiplexer_6_out1), .out2(demultiplexer_6_out2),
    .out3(demultiplexer_6_out3), .in(xor_13_out), .sel(bit_extender_1_out[8:7]));
  xor xor_13 (xor_13_out, or_14_out, ALU_Reg_Status[2]);
  and and_23 (and_23_out, ALU_Reg_Status[2], or_14_out);
  or or_13 (ALU_Reg_Status[2], and_30_out, and_28_out, bit_extender_1_out[5]);
  or or_14 (or_14_out, and_24_out, xor_14_out);
  and and_24 (and_24_out, xor_15_out, bit_extender_1_out[4], xor_16_out);
  xor xor_14 (xor_14_out, xor_16_out, xor_15_out);
  and and_25 (and_25_out, xor_16_out, xor_15_out);
  xor xor_15 (xor_15_out, and_26_out, bit_extender_1_out[2]);
  xor xor_16 (xor_16_out, and_27_out, bit_extender_1_out[3]);
  and and_26 (and_26_out, Reg_ALU_A[4], bit_extender_1_out[0]);
  and and_27 (and_27_out, Reg_ALU_B[4], bit_extender_1_out[1]);
  or or_15 (ALU_Reg_C[3], demultiplexer_7_out0, demultiplexer_8_out1, demultiplexer_6_out2);
  Demultiplexer #(.select(2), .enable("false")) demultiplexer_7 (
    .out0(demultiplexer_7_out0), .out1(demultiplexer_7_out1), .out2(demultiplexer_7_out2),
    .out3(demultiplexer_7_out3), .in(xor_17_out), .sel(bit_extender_1_out[8:7]));
  xor xor_17 (xor_17_out, or_17_out, or_16_out);
  and and_28 (and_28_out, or_16_out, or_17_out);
  or or_16 (or_16_out, and_35_out, and_33_out, bit_extender_1_out[5]);
  or or_17 (or_17_out, and_29_out, xor_18_out);
  and and_29 (and_29_out, xor_19_out, bit_extender_1_out[4], xor_20_out);
  xor xor_18 (xor_18_out, xor_20_out, xor_19_out);
  and and_30 (and_30_out, xor_20_out, xor_19_out);
  xor xor_19 (xor_19_out, and_31_out, bit_extender_1_out[2]);
  xor xor_20 (xor_20_out, and_32_out, bit_extender_1_out[3]);
  and and_31 (and_31_out, Reg_ALU_A[3], bit_extender_1_out[0]);
  and and_32 (and_32_out, Reg_ALU_B[3], bit_extender_1_out[1]);
  or or_18 (ALU_Reg_C[2], demultiplexer_8_out0, demultiplexer_9_out1, demultiplexer_7_out2);
  Demultiplexer #(.select(2), .enable("false")) demultiplexer_8 (
    .out0(demultiplexer_8_out0), .out1(demultiplexer_8_out1), .out2(demultiplexer_8_out2),
    .out3(demultiplexer_8_out3), .in(xor_21_out), .sel(bit_extender_1_out[8:7]));
  xor xor_21 (xor_21_out, or_20_out, or_19_out);
  and and_33 (and_33_out, or_19_out, or_20_out);
  or or_19 (or_19_out, and_40_out, and_38_out, bit_extender_1_out[5]);
  or or_20 (or_20_out, and_34_out, xor_22_out);
  and and_34 (and_34_out, xor_25_out, bit_extender_1_out[4], xor_23_out);
  xor xor_22 (xor_22_out, xor_23_out, xor_25_out);
  and and_35 (and_35_out, xor_23_out, xor_25_out);
  xor xor_23 (xor_23_out, and_37_out, bit_extender_1_out[3]);
  and and_36 (and_36_out, Reg_ALU_A[2], bit_extender_1_out[0]);
  and and_37 (and_37_out, Reg_ALU_B[2], bit_extender_1_out[1]);
  or or_21 (ALU_Reg_C[1], demultiplexer_9_out0, demultiplexer_10_out1, demultiplexer_8_out2);
  Demultiplexer #(.select(2), .enable("false")) demultiplexer_9 (
    .out0(demultiplexer_9_out0), .out1(demultiplexer_9_out1), .out2(demultiplexer_9_out2),
    .out3(demultiplexer_9_out3), .in(xor_24_out), .sel(bit_extender_1_out[8:7]));
  xor xor_24 (xor_24_out, or_23_out, or_22_out);
  and and_38 (and_38_out, or_22_out, or_23_out);
  or or_22 (or_22_out, and_44_out, and_42_out, bit_extender_1_out[5]);
  or or_23 (or_23_out, and_39_out, xor_27_out);
  and and_39 (and_39_out, xor_29_out, bit_extender_1_out[4], xor_26_out);
  and and_40 (and_40_out, xor_26_out, xor_29_out);
  xor xor_25 (xor_25_out, and_36_out, bit_extender_1_out[2]);
  xor xor_26 (xor_26_out, and_41_out, bit_extender_1_out[3]);
  and and_41 (and_41_out, Reg_ALU_B[1], bit_extender_1_out[1]);
  or or_24 (ALU_Reg_C[0], demultiplexer_10_out0, demultiplexer_9_out2, demultiplexer_1_out1);
  and and_42 (and_42_out, or_25_out, or_26_out);
  and and_43 (and_43_out, xor_32_out, bit_extender_1_out[4], xor_28_out);
  xor xor_27 (xor_27_out, xor_26_out, xor_29_out);
  and and_44 (and_44_out, xor_28_out, xor_32_out);
  xor xor_28 (xor_28_out, and_46_out, bit_extender_1_out[3]);
  xor xor_29 (xor_29_out, and_45_out, bit_extender_1_out[2]);
  and and_45 (and_45_out, Reg_ALU_A[1], bit_extender_1_out[0]);
  and and_46 (and_46_out, Reg_ALU_B[0], bit_extender_1_out[1]);
  Demultiplexer #(.select(2), .enable("false")) demultiplexer_10 (
    .out0(demultiplexer_10_out0), .out1(demultiplexer_10_out1), .out2(demultiplexer_10_out2),
    .out3(demultiplexer_10_out3), .in(xor_30_out), .sel(bit_extender_1_out[8:7]));
  xor xor_30 (xor_30_out, or_26_out, or_25_out);
  or or_25 (or_25_out, bit_extender_1_out[6], bit_extender_1_out[5]);
  or or_26 (or_26_out, and_43_out, xor_31_out);
  xor xor_31 (xor_31_out, xor_28_out, xor_32_out);
  xor xor_32 (xor_32_out, and_47_out, bit_extender_1_out[2]);
  and and_47 (and_47_out, Reg_ALU_A[0], bit_extender_1_out[0]);

  // Notes on the sheet:
  //   Roll
  //   A<B
  //   A>B
  //   A=B
  //   Shift
  //   CarryIn
  //   XORSwitch
  //   Invert
  //   Enable
  //   RShift
  //   LShift
  //   4BitCarry
  //   Overflow
  //   Carry
  //   FloodCarry
endmodule

module CPU_CU (
  input  [15:0] ROM_CU_Befehle,
  input  Int_CU_ROMZugriff,
  input  Int_CU_RAMZugriff,
  input  Takt,
  input  [15:0] Reg_CU_Ptr,
  input  IC_CU_Int,
  output [7:0] CU_Reg_Steuerung,
  output CU_Reg_ALUOP,
  output CU_Counter_Branch,
  output CU_RAM_Speicher,
  output CU_RAM_Lade,
  output CU_Out_Sende,
  output CU_MMU_SetzeTLB,
  output CU_IC_SetzteInt,
  output CU_IC_Interrupt,
  output CU_Out_SpeicherSpReg,
  output CU_Out_LadeSpReg,
  output CU_Counter_IntCall,
  output [3:0] CU_Out_Sonderargument,
  output [3:0] CU_Ext_Moduladresse,
  output [3:0] CU_Out_Sonderregister,
  output [3:0] CU_MMU_TLBWahl,
  output [7:0] CU_Counter_StatusVergleich,
  output [3:0] CU_ALU_Operation,
  output [7:0] CU_Out_Modus,
  output [7:0] CU_Reg_Wert,
  output [3:0] CU_Reg_Quelladresse,
  output [3:0] CU_Out_Zusatzargument,
  output [3:0] CU_Reg_Zieladresse,
  output CU_Out_Weiter,
  output CU_Out_WeiterZwei,
  output CU_IC_ModeVerletzung,
  output [15:0] CU_Out_CPUModus
);

  wire and_1_out, and_2_out, and_3_out, and_4_out, and_5_out, MaskiereInt_q, or_1_out, or_2_out, or_3_out,
       or_4_out, or_5_out, or_6_out, or_7_out, or_8_out;
  wire [3:0] register_1_q_2, register_1_q_3;
  wire [15:0] controlled_buffer_1_out, register_1_q;
  wire [31:0] rom_1_data;

  Register #(.width(16)) register_1 (
    .D(ROM_CU_Befehle), .en(CU_Out_WeiterZwei), .clk(Takt),
    .Q({register_1_q[15:12], register_1_q_3, register_1_q_2, register_1_q[3:0]}));  // open: clr
  T_Flip_Flop #(.trigger("falling")) t_ff_1 (
    .T(1'b1), .clk(Takt), .Q(CU_Out_Weiter), .Qn(CU_Out_WeiterZwei));  // open: reset, preset
  and and_1 (and_1_out, IC_CU_Int, CU_Out_Weiter);
  ROM #(.addrWidth(4), .dataWidth(32)) rom_1 (
    .addr(register_1_q[15:12]),
    .data({rom_1_data[31:29], CU_Counter_IntCall, CU_Out_LadeSpReg, CU_Out_SpeicherSpReg, CU_IC_Interrupt, CU_IC_SetzteInt, rom_1_data[23], CU_MMU_SetzeTLB, CU_Out_Sende, CU_RAM_Lade, CU_RAM_Speicher, CU_Counter_Branch, CU_Reg_ALUOP, CU_Reg_Steuerung, rom_1_data[8:0]}));
  assign controlled_buffer_1_out = and_4_out ? Reg_CU_Ptr : 16'bz;  // Controlled_Buffer controlled_buffer_1
  Pull_Resistor pull_resistor_1 (.node(controlled_buffer_1_out));
  and and_2 (and_2_out, CU_Out_Weiter, and_4_out);
  and and_3 (and_3_out, CU_Counter_IntCall, CU_Out_Weiter);
  Pull_Resistor pull_resistor_2 (.node(CU_Out_Sonderargument));
  assign CU_Out_Sonderargument = rom_1_data[29] ? register_1_q_3 : 4'bz;  // Controlled_Buffer controlled_buffer_2
  assign CU_Ext_Moduladresse = rom_1_data[23] ? register_1_q_3 : 4'bz;  // Controlled_Buffer controlled_buffer_3
  Pull_Resistor pull_resistor_3 (.node(CU_Ext_Moduladresse));
  Pull_Resistor pull_resistor_4 (.node(CU_Out_Sonderregister));
  assign CU_Out_Sonderregister = rom_1_data[8] ? register_1_q_3 : 4'bz;  // Controlled_Buffer controlled_buffer_4
  Pull_Resistor pull_resistor_5 (.node(CU_MMU_TLBWahl));
  assign CU_MMU_TLBWahl = rom_1_data[7] ? register_1_q_3 : 4'bz;  // Controlled_Buffer controlled_buffer_5
  Pull_Resistor pull_resistor_6 (.node(CU_Counter_StatusVergleich));
  assign CU_Counter_StatusVergleich = rom_1_data[6] ? {register_1_q_3, register_1_q_2} : 8'bz;  // Controlled_Buffer controlled_buffer_6
  Pull_Resistor pull_resistor_7 (.node(CU_ALU_Operation));
  assign CU_ALU_Operation = rom_1_data[5] ? register_1_q_3 : 4'bz;  // Controlled_Buffer controlled_buffer_7
  Pull_Resistor pull_resistor_8 (.node(CU_Out_Modus));
  assign CU_Out_Modus = rom_1_data[4] ? {register_1_q_3, register_1_q_2} : 8'bz;  // Controlled_Buffer controlled_buffer_8
  assign CU_Reg_Wert = rom_1_data[3] ? {register_1_q_3, register_1_q_2} : 8'bz;  // Controlled_Buffer controlled_buffer_9
  Pull_Resistor pull_resistor_9 (.node(CU_Reg_Wert));
  Pull_Resistor pull_resistor_10 (.node(CU_Reg_Quelladresse));
  assign CU_Reg_Quelladresse = rom_1_data[2] ? register_1_q_2 : 4'bz;  // Controlled_Buffer controlled_buffer_10
  Pull_Resistor pull_resistor_11 (.node(CU_Out_Zusatzargument));
  assign CU_Out_Zusatzargument = rom_1_data[1] ? register_1_q[3:0] : 4'bz;  // Controlled_Buffer controlled_buffer_11
  assign CU_Reg_Zieladresse = rom_1_data[0] ? register_1_q[3:0] : 4'bz;  // Controlled_Buffer controlled_buffer_12
  Pull_Resistor pull_resistor_12 (.node(CU_Reg_Zieladresse));
  and and_4 (and_4_out, CU_Out_SpeicherSpReg, CU_Out_Sonderregister[1]);
  or or_1 (or_1_out, and_2_out, and_3_out, and_1_out);
  or or_2 (or_2_out, controlled_buffer_1_out[1], CU_Out_Sonderargument[1]);
  or or_3 (or_3_out, and_2_out, and_1_out, and_3_out);
  or or_4 (or_4_out, and_2_out, and_1_out);
  or or_5 (or_5_out, and_2_out, CU_Out_Sonderargument[3], and_1_out);
  Register #(.width(1), .trigger("falling")) TLB (
    .D(or_6_out), .en(or_1_out), .clk(Takt), .Q(CU_Out_CPUModus[0]));  // open: clr
  or or_6 (or_6_out, CU_Out_Sonderargument[0], controlled_buffer_1_out[0]);
  Register #(.width(1), .trigger("falling")) Modus (
    .D(and_5_out), .en(or_3_out), .clk(Takt), .Q(CU_Out_CPUModus[1]));  // open: clr
  and and_5 (and_5_out, ~and_1_out, or_2_out);  // AND_Gate
  Register #(.width(1), .trigger("falling")) TimerInt (
    .D(or_7_out), .en(or_4_out), .clk(Takt), .Q(CU_Out_CPUModus[2]));  // open: clr
  or or_7 (or_7_out, CU_Out_Sonderargument[2], controlled_buffer_1_out[2]);
  Register #(.width(1), .trigger("falling")) MaskiereInt (
    .D(or_8_out), .en(or_5_out), .clk(Takt), .Q(MaskiereInt_q));  // open: clr
  or or_8 (or_8_out, CU_Out_Sonderargument[3], controlled_buffer_1_out[3]);
  and and_6 (CU_Out_CPUModus[3], ~CU_IC_Interrupt, MaskiereInt_q);  // AND_Gate
  and and_7 (CU_IC_ModeVerletzung, rom_1_data[31], CU_Out_CPUModus[1]);
  Pull_Resistor pull_resistor_13 (.node(CU_Out_CPUModus));

  // Notes on the sheet:
  //   contents of rom_1 (hex, n*v repeats v):
  //   0 14009 6005 3c021 400 82004 10c001 81002004 2003004 40040 800 b0000000 80402084 88000900 84000100
  //   80202004
endmodule

module CPU_Register (
  input  [7:0] CU_Reg_Steuerung,
  input  [7:0] CU_Reg_RegAdressen,
  input  [7:0] Out_Reg_Wert,
  input  [7:0] CU_Reg_Wert,
  input  [7:0] ALU_Reg_C,
  input  [15:0] Out_Reg_Adresse,
  input  CU_Reg_ALUOP,
  input  Takt,
  input  [7:0] ALU_Reg_Status,
  input  CU_Reg_WeiterZwei,
  input  CU_Reg_Weiter,
  input  IC_Reg_Interrupt,
  input  [15:0] CU_Reg_Modus,
  input  CU_Reg_SetzteSonderReg,
  input  CU_Reg_LadeSonderReg,
  input  [3:0] CU_Reg_SonderReg,
  output [7:0] Reg_Out_Daten,
  output [15:0] Reg_Out_Pointer,
  output [15:0] Reg_Counter_IntCallAdr,
  output [7:0] Reg_Counter_Status,
  output [7:0] Reg_ALU_A,
  output [7:0] Reg_ALU_B,
  output Reg_IC_KernelReg,
  output Reg_Out_LadeStatus
);

  wire and_1_out, and_2_out, and_3_out, and_5_out, and_6_out, and_7_out, and_8_out, and_9_out, and_10_out,
       and_11_out, and_12_out, and_13_out, decoder_1_out0, decoder_1_out1, decoder_1_out2, decoder_1_out3,
       decoder_1_out4, decoder_1_out5, decoder_1_out6, decoder_1_out7, decoder_1_out8, decoder_1_out9,
       decoder_1_out10, decoder_1_out11, decoder_1_out12, decoder_1_out13, decoder_1_out14, decoder_1_out15,
       not_1_out, or_1_out, or_2_out, or_3_out, or_4_out, or_5_out, or_6_out, or_7_out;
  wire [7:0] Ac8_q, C8_q, controlled_buffer_1_out, controlled_buffer_2_out, controlled_buffer_3_out,
       controlled_buffer_4_out, D8_q, E8_q, F8_q, G8_q, IH8_q, IL8_q, multiplexer_1_out, multiplexer_2_out,
       multiplexer_3_out, multiplexer_4_out, multiplexer_5_out, multiplexer_6_out, SA8_q, SB8_q, SC8_q, SD8_q;

  Multiplexer #(.select(2), .width(8), .enable("false")) multiplexer_1 (
    .in0(Reg_Out_Daten), .in1(Out_Reg_Wert), .in2(CU_Reg_Wert), .in3(ALU_Reg_C), .out(multiplexer_1_out),
    .sel(CU_Reg_Steuerung[7:6]));
  not not_1 (not_1_out, CU_Reg_Modus[1]);
  and and_1 (and_1_out, CU_Reg_Weiter, CU_Reg_Steuerung[5]);
  Decoder #(.select(4)) decoder_1 (
    .out0(decoder_1_out0), .out1(decoder_1_out1), .out2(decoder_1_out2), .out3(decoder_1_out3),
    .out4(decoder_1_out4), .out5(decoder_1_out5), .out6(decoder_1_out6), .out7(decoder_1_out7),
    .out8(decoder_1_out8), .out9(decoder_1_out9), .out10(decoder_1_out10), .out11(decoder_1_out11),
    .out12(decoder_1_out12), .out13(decoder_1_out13), .out14(decoder_1_out14), .out15(decoder_1_out15),
    .sel(CU_Reg_RegAdressen[3:0]), .en(and_1_out));
  Multiplexer #(.width(8), .enable("false")) multiplexer_2 (
    .in0(ALU_Reg_Status), .in1(Reg_Out_Pointer[7:0]), .out(multiplexer_2_out), .sel(and_3_out));
  and and_2 (and_2_out, CU_Reg_Weiter, or_1_out);
  or or_1 (or_1_out, and_3_out, CU_Reg_ALUOP);
  and and_3 (and_3_out, CU_Reg_SonderReg[3], CU_Reg_SetzteSonderReg);
  and and_4 (Reg_Out_LadeStatus, CU_Reg_LadeSonderReg, CU_Reg_SonderReg[3]);
  Register #(.trigger("falling")) Ac8 (
    .D(multiplexer_1_out), .en(decoder_1_out0), .clk(Takt), .Q(Ac8_q), .clr(CU_Reg_Steuerung[1]));
  Register #(.trigger("falling")) A8 (
    .D(multiplexer_1_out), .en(decoder_1_out1), .clk(Takt), .Q(Reg_ALU_A), .clr(CU_Reg_Steuerung[1]));
  Register #(.trigger("falling")) B8 (
    .D(multiplexer_1_out), .en(decoder_1_out2), .clk(Takt), .Q(Reg_ALU_B), .clr(CU_Reg_Steuerung[1]));
  Register #(.trigger("falling")) C8 (
    .D(multiplexer_1_out), .en(decoder_1_out3), .clk(Takt), .Q(C8_q), .clr(CU_Reg_Steuerung[1]));
  Register #(.trigger("falling")) D8 (
    .D(multiplexer_1_out), .en(decoder_1_out4), .clk(Takt), .Q(D8_q), .clr(CU_Reg_Steuerung[1]));
  Register #(.trigger("falling")) E8 (
    .D(multiplexer_1_out), .en(decoder_1_out5), .clk(Takt), .Q(E8_q), .clr(CU_Reg_Steuerung[1]));
  Register #(.trigger("falling")) F8 (
    .D(multiplexer_1_out), .en(decoder_1_out6), .clk(Takt), .Q(F8_q), .clr(CU_Reg_Steuerung[1]));
  Register #(.trigger("falling")) G8 (
    .D(multiplexer_1_out), .en(decoder_1_out7), .clk(Takt), .Q(G8_q), .clr(CU_Reg_Steuerung[1]));
  Register #(.trigger("falling")) Status (
    .D(multiplexer_2_out), .en(and_2_out), .clk(Takt), .Q(Reg_Counter_Status), .clr(or_2_out));
  or or_2 (or_2_out, CU_Reg_Steuerung[1], CU_Reg_Steuerung[0]);
  and and_5 (and_5_out, CU_Reg_WeiterZwei, CU_Reg_Steuerung[2]);
  and and_6 (and_6_out, CU_Reg_WeiterZwei, CU_Reg_Steuerung[3]);
  and and_7 (and_7_out, CU_Reg_WeiterZwei, ~CU_Reg_Steuerung[3], IC_Reg_Interrupt);  // AND_Gate
  or or_3 (or_3_out, and_7_out, and_6_out);
  Multiplexer #(.width(8), .enable("false")) multiplexer_3 (
    .in0(multiplexer_1_out), .in1(Out_Reg_Adresse[7:0]), .out(multiplexer_3_out), .sel(and_5_out));
  Multiplexer #(.width(8), .enable("false")) multiplexer_4 (
    .in0(multiplexer_1_out), .in1(Out_Reg_Adresse[15:8]), .out(multiplexer_4_out), .sel(and_5_out));
  Multiplexer #(.width(8), .enable("false")) multiplexer_5 (
    .in0(multiplexer_1_out), .in1(Out_Reg_Adresse[7:0]), .out(multiplexer_5_out), .sel(or_3_out));
  and and_8 (and_8_out, decoder_1_out14, not_1_out);
  Multiplexer #(.width(8), .enable("false")) multiplexer_6 (
    .in0(multiplexer_1_out), .in1(Out_Reg_Adresse[15:8]), .out(multiplexer_6_out), .sel(or_3_out));
  and and_9 (and_9_out, decoder_1_out15, not_1_out);
  Register #(.trigger("falling")) SA8 (
    .D(multiplexer_1_out), .en(and_10_out), .clk(Takt), .Q(SA8_q), .clr(CU_Reg_Steuerung[0]));
  and and_10 (and_10_out, decoder_1_out8, not_1_out);
  Register #(.trigger("falling")) SB8 (
    .D(multiplexer_1_out), .en(and_11_out), .clk(Takt), .Q(SB8_q), .clr(CU_Reg_Steuerung[0]));
  and and_11 (and_11_out, decoder_1_out9, not_1_out);
  Register #(.trigger("falling")) SC8 (
    .D(multiplexer_1_out), .en(and_12_out), .clk(Takt), .Q(SC8_q), .clr(CU_Reg_Steuerung[0]));
  and and_12 (and_12_out, decoder_1_out10, not_1_out);
  Register #(.trigger("falling")) SD8 (
    .D(multiplexer_1_out), .en(and_13_out), .clk(Takt), .Q(SD8_q), .clr(CU_Reg_Steuerung[0]));
  and and_13 (and_13_out, decoder_1_out11, not_1_out);
  Register #(.trigger("falling")) PL8 (
    .D(multiplexer_3_out), .en(or_4_out), .clk(Takt), .Q(Reg_Out_Pointer[7:0]), .clr(CU_Reg_Steuerung[1]));
  or or_4 (or_4_out, and_5_out, decoder_1_out12);
  Register #(.trigger("falling")) PH8 (
    .D(multiplexer_4_out), .en(or_5_out), .clk(Takt), .Q(Reg_Out_Pointer[15:8]), .clr(CU_Reg_Steuerung[1]));
  or or_5 (or_5_out, and_5_out, decoder_1_out13);
  Register #(.trigger("falling")) IL8 (.D(multiplexer_5_out), .en(or_6_out), .clk(Takt), .Q(IL8_q));  // open: clr
  or or_6 (or_6_out, or_3_out, and_8_out);
  Register #(.trigger("falling")) IH8 (.D(multiplexer_6_out), .en(or_7_out), .clk(Takt), .Q(IH8_q));  // open: clr
  or or_7 (or_7_out, or_3_out, and_9_out);
  assign controlled_buffer_1_out = not_1_out ? SA8_q : 8'bz;  // Controlled_Buffer controlled_buffer_1
  Pull_Resistor pull_resistor_1 (.node(controlled_buffer_1_out));
  assign controlled_buffer_2_out = not_1_out ? SB8_q : 8'bz;  // Controlled_Buffer controlled_buffer_2
  Pull_Resistor pull_resistor_2 (.node(controlled_buffer_2_out));
  assign controlled_buffer_3_out = not_1_out ? SC8_q : 8'bz;  // Controlled_Buffer controlled_buffer_3
  Pull_Resistor pull_resistor_3 (.node(controlled_buffer_3_out));
  assign controlled_buffer_4_out = not_1_out ? SD8_q : 8'bz;  // Controlled_Buffer controlled_buffer_4
  Pull_Resistor pull_resistor_4 (.node(controlled_buffer_4_out));
  assign Reg_Counter_IntCallAdr[7:0] = not_1_out ? IL8_q : 8'bz;  // Controlled_Buffer controlled_buffer_5
  Pull_Resistor pull_resistor_5 (.node(Reg_Counter_IntCallAdr[7:0]));
  assign Reg_Counter_IntCallAdr[15:8] = not_1_out ? IH8_q : 8'bz;  // Controlled_Buffer controlled_buffer_6
  Pull_Resistor pull_resistor_6 (.node(Reg_Counter_IntCallAdr[15:8]));
  Multiplexer #(.select(4), .width(8)) multiplexer_7 (
    .in0(Ac8_q), .in1(Reg_ALU_A), .in2(Reg_ALU_B), .in3(C8_q), .in4(D8_q), .in5(E8_q), .in6(F8_q),
    .in7(G8_q), .in8(controlled_buffer_1_out), .in9(controlled_buffer_2_out), .in10(controlled_buffer_3_out),
    .in11(controlled_buffer_4_out), .in12(Reg_Out_Pointer[7:0]), .in13(Reg_Out_Pointer[15:8]),
    .in14(Reg_Counter_IntCallAdr[7:0]), .in15(Reg_Counter_IntCallAdr[15:8]), .out(Reg_Out_Daten),
    .sel(CU_Reg_RegAdressen[7:4]), .en(CU_Reg_Steuerung[4]));
  or or_8 (Reg_IC_KernelReg, decoder_1_out15, decoder_1_out14, decoder_1_out11, decoder_1_out10, decoder_1_out9, decoder_1_out8);
endmodule

module CPU_Counter (
  input  [15:0] Reg_Counter_Pointer,
  input  [15:0] Reg_Counter_IntCall,
  input  [15:0] IC_Counter_IntPtr,
  input  Takt,
  input  CU_Counter_Weiter,
  input  CU_Counter_Branch,
  input  CU_Counter_IntCallPtr,
  input  IC_Counter_Int,
  input  [7:0] Reg_Counter_Status,
  input  [7:0] CU_Counter_Status,
  input  Out_Counter_Reset,
  output [15:0] Counter_Reg_AdressePE,
  output [15:0] Counter_MMU_Adresse
);

  wire and_2_out, and_3_out, and_4_out, nor_1_out, not_1_out, or_1_out, or_2_out, or_3_out;
  wire [1:0] or_4_out, pull_resistor_1_node;
  wire [7:0] and_1_out;
  wire [15:0] adder_1_out, multiplexer_1_out, pull_resistor_2_node;

  assign and_1_out = Reg_Counter_Status & CU_Counter_Status;  // AND_Gate and_1, 8 bits wide
  or or_1 (or_1_out, or_2_out, nor_1_out);
  or or_2 (or_2_out, and_1_out[7], and_1_out[6], and_1_out[5], and_1_out[4], and_1_out[3], and_1_out[2], and_1_out[1], and_1_out[0]);
  nor nor_1 (nor_1_out, CU_Counter_Status[7], CU_Counter_Status[6], CU_Counter_Status[5], CU_Counter_Status[4], CU_Counter_Status[3], CU_Counter_Status[2], CU_Counter_Status[1], CU_Counter_Status[0]);
  or or_3 (or_3_out, CU_Counter_Weiter, or_4_out[1], or_4_out[0]);
  and and_2 (and_2_out, CU_Counter_Branch, IC_Counter_Int);
  not not_1 (not_1_out, CU_Counter_Weiter);
  and and_3 (and_3_out, CU_Counter_Branch, ~CU_Counter_IntCallPtr, ~IC_Counter_Int, or_1_out);  // AND_Gate
  and and_4 (and_4_out, ~CU_Counter_Branch, CU_Counter_IntCallPtr, ~IC_Counter_Int);  // AND_Gate
  Multiplexer #(.select(2), .width(16), .enable("false")) multiplexer_1 (
    .in0(adder_1_out), .in1(Reg_Counter_Pointer), .in2(Reg_Counter_IntCall), .in3(IC_Counter_IntPtr),
    .out(multiplexer_1_out), .sel(pull_resistor_1_node));
  Pull_Resistor pull_resistor_1 (.node(pull_resistor_1_node));
  assign pull_resistor_1_node = not_1_out ? or_4_out : 2'bz;  // Controlled_Buffer controlled_buffer_1
  or or_4 (or_4_out[0], and_3_out, IC_Counter_Int);
  or or_5 (or_4_out[1], and_4_out, IC_Counter_Int);
  Register #(.width(16)) register_1 (
    .D(multiplexer_1_out), .en(or_3_out), .clk(Takt), .Q(Counter_MMU_Adresse), .clr(Out_Counter_Reset));
  Pull_Resistor pull_resistor_2 (.node(pull_resistor_2_node));
  Adder #(.width(16)) adder_1 (
    .a(pull_resistor_2_node), .b(Counter_MMU_Adresse), .out(adder_1_out), .cin(1'b1));  // open: cout
  Multiplexer #(.width(16), .enable("false")) multiplexer_2 (
    .in0(Counter_MMU_Adresse), .in1(Reg_Counter_Pointer), .out(Counter_Reg_AdressePE), .sel(and_2_out));
endmodule

module CPU_RAM (
  input  [23:0] Reg_RAM_Pointer,
  input  CU_RAM_Speicher,
  input  CU_RAM_Lade,
  input  Takt,
  input  CU_RAM_Weiter,
  input  [7:0] Reg_RAM_Daten,
  output [7:0] RAM_Reg_Daten
);

  wire and_1_out, and_2_out;
  wire [7:0] ram_1_dout;

  and and_1 (and_1_out, CU_RAM_Weiter, CU_RAM_Lade);
  and and_2 (and_2_out, CU_RAM_Speicher, CU_RAM_Weiter);
  RAM #(.addrWidth(24), .databus("bibus")) ram_1 (
    .addr(Reg_RAM_Pointer), .we(and_2_out), .oe(and_1_out), .clk(Takt), .din(Reg_RAM_Daten), .dout(ram_1_dout));
  assign RAM_Reg_Daten = CU_RAM_Weiter ? ram_1_dout : 8'bz;  // Controlled_Buffer controlled_buffer_1
  Pull_Resistor pull_resistor_1 (.node(RAM_Reg_Daten));
endmodule

module CPU_IC (
  input  [7:0] Out_IC_IntNummer,
  input  [7:0] Reg_IC_IntSaveNummer,
  input  [15:0] Reg_IC_Pointer,
  input  CU_IC_DaisychainEnde,
  input  CU_IC_SetzteInt,
  input  Takt,
  input  CU_IC_TimerWeiterZwei,
  input  CU_IC_SetzteSonderReg,
  input  CU_IC_LadeSonderReg,
  input  Out_IC_Daisychain1A,
  input  [15:0] CU_IC_Modus,
  input  [3:0] CU_IC_SonderReg,
  output [15:0] IC_Counter_Ptr,
  output IC_Out_IntMaskiert,
  output IC_Out_Daisychain1B,
  output [15:0] IC_Reg_SpReg,
  output IC_Out_Interrupt
);

  wire and_1_out, and_2_out, and_3_out, comparator_1_eq, decoder_1_out0, decoder_1_out1, decoder_1_out2,
       decoder_1_out3, decoder_1_out4, decoder_1_out5, decoder_1_out6, decoder_1_out7, decoder_1_out8,
       decoder_1_out9, decoder_1_out10, decoder_1_out11, decoder_1_out12, decoder_1_out13, decoder_1_out14,
       decoder_1_out15, decoder_1_out16, decoder_1_out17, decoder_1_out18, decoder_1_out19, decoder_1_out20,
       decoder_1_out21, decoder_1_out22, decoder_1_out23, decoder_1_out24, decoder_1_out25, decoder_1_out26,
       decoder_1_out27, decoder_1_out28, decoder_1_out29, decoder_1_out30, decoder_1_out31, not_1_out,
       or_1_out;
  wire [3:0] demultiplexer_1_out0, demultiplexer_1_out1;
  wire [4:0] bit_extender_1_out, bit_extender_2_out, or_3_out, pull_resistor_3_node;
  wire [15:0] adder_1_out, InterProzessInt_q, Mod1_q, Mod2_q, Mod3_q, Mod4_q, Mod5_q, Mod6_q, Mod7_q, Mod8_q,
       Mod9_q, Mod10_q, Mod11_q, Mod12_q, Mod13_q, Mod14_q, Mod15_q, Mod16_q, ModeVerletzung_q,
       pull_resistor_1_node, register_1_q, register_2_q, register_3_q, register_4_q, register_5_q,
       register_6_q, register_7_q, register_8_q, register_9_q, register_10_q, register_11_q, register_12_q,
       register_13_q, register_14_q, Syscall_q, TimerInt_q;

  Bit_Extender #(.out_width(5), .\type ("zero")) bit_extender_1 (.in(Reg_IC_IntSaveNummer), .out(bit_extender_1_out));
  or or_1 (or_1_out, CU_IC_SetzteSonderReg, CU_IC_LadeSonderReg);
  Demultiplexer #(.width(4)) demultiplexer_1 (
    .out0(demultiplexer_1_out0), .out1(demultiplexer_1_out1), .in(CU_IC_SonderReg),
    .sel(CU_IC_LadeSonderReg), .en(or_1_out));
  Register #(.width(16)) register_1 (.D(adder_1_out), .en(and_1_out), .clk(Takt), .Q(register_1_q), .clr(not_1_out));
  and and_1 (and_1_out, CU_IC_TimerWeiterZwei, ~comparator_1_eq, CU_IC_Modus[2]);  // AND_Gate
  not not_1 (not_1_out, CU_IC_Modus[2]);
  Register #(.width(16)) register_2 (
    .D(Reg_IC_Pointer), .en(demultiplexer_1_out0[0]), .clk(Takt), .Q(register_2_q));  // open: clr
  Pull_Resistor pull_resistor_1 (.node(pull_resistor_1_node));
  assign IC_Reg_SpReg = demultiplexer_1_out1[0] ? register_2_q : 16'bz;  // Controlled_Buffer controlled_buffer_1
  Pull_Resistor pull_resistor_2 (.node(IC_Reg_SpReg));
  Adder #(.width(16)) adder_1 (
    .a(pull_resistor_1_node), .b(register_1_q), .out(adder_1_out), .cin(1'b1));  // open: cout
  Comparator #(.width(16), .mode("unsigned")) comparator_1 (
    .a(register_1_q), .b(register_2_q), .eq(comparator_1_eq));  // open: gt, lt
  and and_2 (and_2_out, comparator_1_eq, CU_IC_Modus[2]);
  and and_3 (and_3_out, ~Out_IC_Daisychain1A, CU_IC_Modus[3], and_2_out);  // AND_Gate
  or or_2 (IC_Out_Daisychain1B, Out_IC_Daisychain1A, and_3_out);
  Bit_Extender #(.out_width(5), .\type ("zero")) bit_extender_2 (.in(Out_IC_IntNummer), .out(bit_extender_2_out));
  Pull_Resistor pull_resistor_3 (.node(pull_resistor_3_node));
  assign pull_resistor_3_node = and_3_out ? 5'b11011 : 5'bz;  // Controlled_Buffer controlled_buffer_2
  assign or_3_out = bit_extender_2_out | pull_resistor_3_node;  // OR_Gate or_3, 5 bits wide
  Decoder #(.select(5)) decoder_1 (
    .out0(decoder_1_out0), .out1(decoder_1_out1), .out2(decoder_1_out2), .out3(decoder_1_out3),
    .out4(decoder_1_out4), .out5(decoder_1_out5), .out6(decoder_1_out6), .out7(decoder_1_out7),
    .out8(decoder_1_out8), .out9(decoder_1_out9), .out10(decoder_1_out10), .out11(decoder_1_out11),
    .out12(decoder_1_out12), .out13(decoder_1_out13), .out14(decoder_1_out14), .out15(decoder_1_out15),
    .out16(decoder_1_out16), .out17(decoder_1_out17), .out18(decoder_1_out18), .out19(decoder_1_out19),
    .out20(decoder_1_out20), .out21(decoder_1_out21), .out22(decoder_1_out22), .out23(decoder_1_out23),
    .out24(decoder_1_out24), .out25(decoder_1_out25), .out26(decoder_1_out26), .out27(decoder_1_out27),
    .out28(decoder_1_out28), .out29(decoder_1_out29), .out30(decoder_1_out30), .out31(decoder_1_out31),
    .sel(bit_extender_1_out), .en(CU_IC_SetzteInt));
  Register #(.width(16)) Mod1 (.D(Reg_IC_Pointer), .en(decoder_1_out0), .clk(Takt), .Q(Mod1_q));  // open: clr
  Register #(.width(16)) Mod2 (.D(Reg_IC_Pointer), .en(decoder_1_out1), .clk(Takt), .Q(Mod2_q));  // open: clr
  Register #(.width(16)) Mod3 (.D(Reg_IC_Pointer), .en(decoder_1_out2), .clk(Takt), .Q(Mod3_q));  // open: clr
  Register #(.width(16)) Mod4 (.D(Reg_IC_Pointer), .en(decoder_1_out3), .clk(Takt), .Q(Mod4_q));  // open: clr
  Register #(.width(16)) Mod5 (.D(Reg_IC_Pointer), .en(decoder_1_out4), .clk(Takt), .Q(Mod5_q));  // open: clr
  Register #(.width(16)) Mod6 (.D(Reg_IC_Pointer), .en(decoder_1_out5), .clk(Takt), .Q(Mod6_q));  // open: clr
  Register #(.width(16)) Mod7 (.D(Reg_IC_Pointer), .en(decoder_1_out6), .clk(Takt), .Q(Mod7_q));  // open: clr
  Register #(.width(16)) Mod8 (.D(Reg_IC_Pointer), .en(decoder_1_out7), .clk(Takt), .Q(Mod8_q));  // open: clr
  Register #(.width(16)) Mod9 (.D(Reg_IC_Pointer), .en(decoder_1_out8), .clk(Takt), .Q(Mod9_q));  // open: clr
  Register #(.width(16)) Mod10 (.D(Reg_IC_Pointer), .en(decoder_1_out9), .clk(Takt), .Q(Mod10_q));  // open: clr
  Register #(.width(16)) Mod11 (.D(Reg_IC_Pointer), .en(decoder_1_out10), .clk(Takt), .Q(Mod11_q));  // open: clr
  Register #(.width(16)) Mod12 (.D(Reg_IC_Pointer), .en(decoder_1_out11), .clk(Takt), .Q(Mod12_q));  // open: clr
  Register #(.width(16)) Mod13 (.D(Reg_IC_Pointer), .en(decoder_1_out12), .clk(Takt), .Q(Mod13_q));  // open: clr
  Register #(.width(16)) Mod14 (.D(Reg_IC_Pointer), .en(decoder_1_out13), .clk(Takt), .Q(Mod14_q));  // open: clr
  Register #(.width(16)) Mod15 (.D(Reg_IC_Pointer), .en(decoder_1_out14), .clk(Takt), .Q(Mod15_q));  // open: clr
  Register #(.width(16)) Mod16 (.D(Reg_IC_Pointer), .en(decoder_1_out15), .clk(Takt), .Q(Mod16_q));  // open: clr
  Multiplexer #(.select(5), .width(16)) multiplexer_1 (
    .in0(Mod1_q), .in1(Mod2_q), .in2(Mod3_q), .in3(Mod4_q), .in4(Mod5_q), .in5(Mod6_q), .in6(Mod7_q),
    .in7(Mod8_q), .in8(Mod9_q), .in9(Mod10_q), .in10(Mod11_q), .in11(Mod12_q), .in12(Mod13_q),
    .in13(Mod14_q), .in14(Mod15_q), .in15(Mod16_q), .in16(ModeVerletzung_q), .in17(register_3_q),
    .in18(register_4_q), .in19(register_5_q), .in20(register_6_q), .in21(register_7_q), .in22(register_8_q),
    .in23(register_9_q), .in24(register_10_q), .in25(register_11_q), .in26(register_12_q), .in27(TimerInt_q),
    .in28(InterProzessInt_q), .in29(Syscall_q), .in30(register_13_q), .in31(register_14_q),
    .out(IC_Counter_Ptr), .sel(or_3_out), .en(CU_IC_DaisychainEnde));
  Register #(.width(16)) ModeVerletzung (
    .D(Reg_IC_Pointer), .en(decoder_1_out16), .clk(Takt), .Q(ModeVerletzung_q));  // open: clr
  Register #(.width(16)) register_3 (
    .D(Reg_IC_Pointer), .en(decoder_1_out17), .clk(Takt), .Q(register_3_q));  // open: clr
  Register #(.width(16)) register_4 (
    .D(Reg_IC_Pointer), .en(decoder_1_out18), .clk(Takt), .Q(register_4_q));  // open: clr
  Register #(.width(16)) register_5 (
    .D(Reg_IC_Pointer), .en(decoder_1_out19), .clk(Takt), .Q(register_5_q));  // open: clr
  Register #(.width(16)) register_6 (
    .D(Reg_IC_Pointer), .en(decoder_1_out20), .clk(Takt), .Q(register_6_q));  // open: clr
  Register #(.width(16)) register_7 (
    .D(Reg_IC_Pointer), .en(decoder_1_out21), .clk(Takt), .Q(register_7_q));  // open: clr
  Register #(.width(16)) register_8 (
    .D(Reg_IC_Pointer), .en(decoder_1_out22), .clk(Takt), .Q(register_8_q));  // open: clr
  Register #(.width(16)) register_9 (
    .D(Reg_IC_Pointer), .en(decoder_1_out23), .clk(Takt), .Q(register_9_q));  // open: clr
  Register #(.width(16)) register_10 (
    .D(Reg_IC_Pointer), .en(decoder_1_out24), .clk(Takt), .Q(register_10_q));  // open: clr
  Register #(.width(16)) register_11 (
    .D(Reg_IC_Pointer), .en(decoder_1_out25), .clk(Takt), .Q(register_11_q));  // open: clr
  Register #(.width(16)) register_12 (
    .D(Reg_IC_Pointer), .en(decoder_1_out26), .clk(Takt), .Q(register_12_q));  // open: clr
  Register #(.width(16)) TimerInt (.D(Reg_IC_Pointer), .en(decoder_1_out27), .clk(Takt), .Q(TimerInt_q));  // open: clr
  Register #(.width(16)) InterProzessInt (
    .D(Reg_IC_Pointer), .en(decoder_1_out28), .clk(Takt), .Q(InterProzessInt_q));  // open: clr
  Register #(.width(16)) Syscall (.D(Reg_IC_Pointer), .en(decoder_1_out29), .clk(Takt), .Q(Syscall_q));  // open: clr
  Register #(.width(16)) register_13 (
    .D(Reg_IC_Pointer), .en(decoder_1_out30), .clk(Takt), .Q(register_13_q));  // open: clr
  Register #(.width(16)) register_14 (
    .D(Reg_IC_Pointer), .en(decoder_1_out31), .clk(Takt), .Q(register_14_q));  // open: clr

  assign IC_Out_Interrupt = CU_IC_DaisychainEnde;
endmodule

module CPU_MMU (
  input  [15:0] Counter_MMU_Adresse,
  input  [15:0] CU_MMU_Modus,
  input  CU_MMU_Schreibe,
  input  Takt,
  input  CU_MMU_Lesen,
  input  [3:0] CU_MMU_TLBAuswahl,
  input  [7:0] Reg_MMU_TLBAdresse,
  input  [15:0] Reg_MMU_Pointer,
  input  [15:0] Reg_MMU_RAMAdresse,
  input  CU_MMU_SchreibeZeit,
  output [23:0] MMU_ROM_Adresse,
  output [23:0] MMU_RAM_Adresse
);

  wire and_1_out, and_2_out, and_3_out, and_4_out, and_5_out, bit_extender_1_out;
  wire [7:0] demultiplexer_1_out1_2, demultiplexer_2_out1_2, multiplexer_1_out, multiplexer_2_out;
  wire [15:0] demultiplexer_1_out0, demultiplexer_2_out0, ram_1_dout, ram_2_dout;
  wire [15:8] demultiplexer_1_out1, demultiplexer_2_out1;
  wire [23:0] bit_extender_2_out, bit_extender_3_out;

  Demultiplexer #(.width(16), .enable("false")) demultiplexer_1 (
    .out0(demultiplexer_1_out0), .out1({demultiplexer_1_out1, demultiplexer_1_out1_2}),
    .in(Counter_MMU_Adresse), .sel(CU_MMU_Modus[0]));
  Bit_Extender #(.in_width(4), .out_width(1), .\type ("zero")) bit_extender_1 (
    .in(CU_MMU_TLBAuswahl), .out(bit_extender_1_out));
  Demultiplexer #(.width(16), .enable("false")) demultiplexer_2 (
    .out0(demultiplexer_2_out0), .out1({demultiplexer_2_out1, demultiplexer_2_out1_2}),
    .in(Reg_MMU_RAMAdresse), .sel(CU_MMU_Modus[0]));
  and and_1 (and_1_out, CU_MMU_SchreibeZeit, CU_MMU_Schreibe);
  Multiplexer #(.width(8), .enable("false")) multiplexer_1 (
    .in0(demultiplexer_1_out1), .in1(Reg_MMU_TLBAdresse), .out(multiplexer_1_out), .sel(and_1_out));
  Multiplexer #(.width(8), .enable("false")) multiplexer_2 (
    .in0(demultiplexer_2_out1), .in1(Reg_MMU_TLBAdresse), .out(multiplexer_2_out), .sel(and_1_out));
  RAM #(.dataWidth(16), .trigger("falling"), .databus("bibus")) ram_1 (
    .addr(multiplexer_1_out), .we(and_2_out), .oe(and_3_out), .clk(Takt), .din(Reg_MMU_Pointer),
    .dout(ram_1_dout));
  and and_2 (and_2_out, ~bit_extender_1_out, and_1_out);  // AND_Gate
  and and_3 (and_3_out, ~and_1_out, CU_MMU_Lesen);  // AND_Gate
  RAM #(.dataWidth(16), .trigger("falling"), .databus("bibus")) ram_2 (
    .addr(multiplexer_2_out), .we(and_4_out), .oe(and_5_out), .clk(Takt), .din(Reg_MMU_Pointer),
    .dout(ram_2_dout));
  and and_4 (and_4_out, bit_extender_1_out, and_1_out);
  and and_5 (and_5_out, ~and_1_out, CU_MMU_Lesen);  // AND_Gate
  assign bit_extender_2_out = {{8{1'b0}}, demultiplexer_1_out0};  // Bit_Extender bit_extender_2
  assign bit_extender_3_out = {{8{1'b0}}, demultiplexer_2_out0};  // Bit_Extender bit_extender_3
  Multiplexer #(.width(24), .enable("false")) multiplexer_3 (
    .in0(bit_extender_2_out), .in1({ram_1_dout, demultiplexer_1_out1_2}), .out(MMU_ROM_Adresse),
    .sel(CU_MMU_Modus[0]));
  Multiplexer #(.width(24), .enable("false")) multiplexer_4 (
    .in0(bit_extender_3_out), .in1({ram_2_dout, demultiplexer_2_out1_2}), .out(MMU_RAM_Adresse),
    .sel(CU_MMU_Modus[0]));
endmodule

module GPU_coming_soon (
);

  wire gpu_alu_1_agleichb, gpu_alu_1_agroesserb, gpu_alu_1_akleinerb, gpu_alu_1_carry, gpu_alu_1_negativ,
       gpu_alu_2_agleichb, gpu_alu_2_agroesserb, gpu_alu_2_akleinerb, gpu_alu_2_carry, gpu_alu_2_negativ,
       gpu_alu_3_agleichb, gpu_alu_3_agroesserb, gpu_alu_3_akleinerb, gpu_alu_3_carry, gpu_alu_3_negativ,
       gpu_alu_4_agleichb, gpu_alu_4_agroesserb, gpu_alu_4_akleinerb, gpu_alu_4_carry, gpu_alu_4_negativ;
  wire [7:0] gpu_alu_1_alu_reg_c, gpu_alu_2_alu_reg_c, gpu_alu_3_alu_reg_c, gpu_alu_4_alu_reg_c,
       gpu_register_1_reg_alu_a, gpu_register_1_reg_alu_b, gpu_register_2_reg_alu_a,
       gpu_register_2_reg_alu_b, gpu_register_3_reg_alu_a, gpu_register_3_reg_alu_b,
       gpu_register_4_reg_alu_a, gpu_register_4_reg_alu_b;

  GPU_ALU gpu_alu_1 (
    .AgleichB(gpu_alu_1_agleichb), .AgroesserB(gpu_alu_1_agroesserb), .Negativ(gpu_alu_1_negativ),
    .Carry(gpu_alu_1_carry), .Reg_ALU_B(gpu_register_1_reg_alu_b), .Reg_ALU_A(gpu_register_1_reg_alu_a),
    .AkleinerB(gpu_alu_1_akleinerb), .ALU_Reg_C(gpu_alu_1_alu_reg_c));  // open: CU_ALU_OPWahl, CU_ALU_OP
  GPU_Register gpu_register_1 (
    .Reg_ALU_A(gpu_register_1_reg_alu_a), .ALU_Reg_C(gpu_alu_1_alu_reg_c),
    .Reg_ALU_B(gpu_register_1_reg_alu_b), .Carry(gpu_alu_1_carry), .Negativ(gpu_alu_1_negativ),
    .AgroesserB(gpu_alu_1_agroesserb), .AgleichB(gpu_alu_1_agleichb), .AkleinerB(gpu_alu_1_akleinerb));  // open: Reg_RAM_Daten, Takt, CU_Reg_Steuerung, RAM_Reg_Wert, CU_Reg_Wert, CU_Reg_Adresse, Reg_Out_Daten, Reg_CU_Status, Reg_Out_Adr
  GPU_ALU gpu_alu_2 (
    .AgleichB(gpu_alu_2_agleichb), .AgroesserB(gpu_alu_2_agroesserb), .Negativ(gpu_alu_2_negativ),
    .Carry(gpu_alu_2_carry), .Reg_ALU_B(gpu_register_2_reg_alu_b), .Reg_ALU_A(gpu_register_2_reg_alu_a),
    .AkleinerB(gpu_alu_2_akleinerb), .ALU_Reg_C(gpu_alu_2_alu_reg_c));  // open: CU_ALU_OPWahl, CU_ALU_OP
  GPU_Register gpu_register_2 (
    .Reg_ALU_A(gpu_register_2_reg_alu_a), .ALU_Reg_C(gpu_alu_2_alu_reg_c),
    .Reg_ALU_B(gpu_register_2_reg_alu_b), .Carry(gpu_alu_2_carry), .Negativ(gpu_alu_2_negativ),
    .AgroesserB(gpu_alu_2_agroesserb), .AgleichB(gpu_alu_2_agleichb), .AkleinerB(gpu_alu_2_akleinerb));  // open: Reg_RAM_Daten, Takt, CU_Reg_Steuerung, RAM_Reg_Wert, CU_Reg_Wert, CU_Reg_Adresse, Reg_Out_Daten, Reg_CU_Status, Reg_Out_Adr
  GPU_ALU gpu_alu_3 (
    .AgleichB(gpu_alu_3_agleichb), .AgroesserB(gpu_alu_3_agroesserb), .Negativ(gpu_alu_3_negativ),
    .Carry(gpu_alu_3_carry), .Reg_ALU_B(gpu_register_3_reg_alu_b), .Reg_ALU_A(gpu_register_3_reg_alu_a),
    .AkleinerB(gpu_alu_3_akleinerb), .ALU_Reg_C(gpu_alu_3_alu_reg_c));  // open: CU_ALU_OPWahl, CU_ALU_OP
  GPU_Register gpu_register_3 (
    .Reg_ALU_A(gpu_register_3_reg_alu_a), .ALU_Reg_C(gpu_alu_3_alu_reg_c),
    .Reg_ALU_B(gpu_register_3_reg_alu_b), .Carry(gpu_alu_3_carry), .Negativ(gpu_alu_3_negativ),
    .AgroesserB(gpu_alu_3_agroesserb), .AgleichB(gpu_alu_3_agleichb), .AkleinerB(gpu_alu_3_akleinerb));  // open: Reg_RAM_Daten, Takt, CU_Reg_Steuerung, RAM_Reg_Wert, CU_Reg_Wert, CU_Reg_Adresse, Reg_Out_Daten, Reg_CU_Status, Reg_Out_Adr
  GPU_ALU gpu_alu_4 (
    .AgleichB(gpu_alu_4_agleichb), .AgroesserB(gpu_alu_4_agroesserb), .Negativ(gpu_alu_4_negativ),
    .Carry(gpu_alu_4_carry), .Reg_ALU_B(gpu_register_4_reg_alu_b), .Reg_ALU_A(gpu_register_4_reg_alu_a),
    .AkleinerB(gpu_alu_4_akleinerb), .ALU_Reg_C(gpu_alu_4_alu_reg_c));  // open: CU_ALU_OPWahl, CU_ALU_OP
  GPU_Register gpu_register_4 (
    .Reg_ALU_A(gpu_register_4_reg_alu_a), .ALU_Reg_C(gpu_alu_4_alu_reg_c),
    .Reg_ALU_B(gpu_register_4_reg_alu_b), .Carry(gpu_alu_4_carry), .Negativ(gpu_alu_4_negativ),
    .AgroesserB(gpu_alu_4_agroesserb), .AgleichB(gpu_alu_4_agleichb), .AkleinerB(gpu_alu_4_akleinerb));  // open: Reg_RAM_Daten, Takt, CU_Reg_Steuerung, RAM_Reg_Wert, CU_Reg_Wert, CU_Reg_Adresse, Reg_Out_Daten, Reg_CU_Status, Reg_Out_Adr
endmodule

module GPU_ALU (
  input  CU_ALU_OP,
  input  [3:0] CU_ALU_OPWahl,
  input  [7:0] Reg_ALU_A,
  input  [7:0] Reg_ALU_B,
  output Carry,
  output Negativ,
  output AgroesserB,
  output AgleichB,
  output AkleinerB,
  output [7:0] ALU_Reg_C
);

  wire adder_1_cout, adder_2_cout, and_2_out, and_3_out, and_4_out, and_7_out, subtractor_1_bout,
       subtractor_2_bout;
  wire [7:0] adder_1_out, adder_2_out, and_1_out, divider_1_out, divider_1_rem, multiplier_1_cout,
       multiplier_1_out, nand_1_out, negator_1_out, nor_1_out, not_1_out, or_1_out, pull_resistor_1_node,
       pull_resistor_2_node, subtractor_1_out, subtractor_2_out, xnor_1_out, xor_1_out;

  Adder adder_1 (.a(Reg_ALU_A), .b(pull_resistor_1_node), .out(adder_1_out), .cin(1'b1), .cout(adder_1_cout));
  Pull_Resistor pull_resistor_1 (.node(pull_resistor_1_node));
  Subtractor subtractor_1 (
    .a(Reg_ALU_A), .b(pull_resistor_2_node), .out(subtractor_1_out), .bin(1'b1), .bout(subtractor_1_bout));
  Pull_Resistor pull_resistor_2 (.node(pull_resistor_2_node));
  Adder adder_2 (.a(Reg_ALU_A), .b(Reg_ALU_B), .out(adder_2_out), .cout(adder_2_cout));  // open: cin
  Subtractor subtractor_2 (
    .a(Reg_ALU_A), .b(Reg_ALU_B), .out(subtractor_2_out), .bout(subtractor_2_bout));  // open: bin
  Multiplier multiplier_1 (
    .a(Reg_ALU_A), .b(Reg_ALU_B), .out(multiplier_1_out), .cout(multiplier_1_cout));  // open: cin
  Divider divider_1 (.a(Reg_ALU_A), .b(Reg_ALU_B), .out(divider_1_out), .rem(divider_1_rem));  // open: upper
  assign not_1_out = ~Reg_ALU_A;  // NOT_Gate not_1, 8 bits wide
  assign and_1_out = Reg_ALU_A & Reg_ALU_B;  // AND_Gate and_1, 8 bits wide
  assign or_1_out = Reg_ALU_A | Reg_ALU_B;  // OR_Gate or_1, 8 bits wide
  assign xor_1_out = Reg_ALU_A ^ Reg_ALU_B;  // XOR_Gate xor_1, 8 bits wide
  Negator negator_1 (.in(Reg_ALU_A), .out(negator_1_out));
  assign xnor_1_out = ~(Reg_ALU_A ^ Reg_ALU_B);  // XNOR_Gate xnor_1, 8 bits wide
  assign nor_1_out = ~(Reg_ALU_A | Reg_ALU_B);  // NOR_Gate nor_1, 8 bits wide
  assign nand_1_out = ~(Reg_ALU_A & Reg_ALU_B);  // NAND_Gate nand_1, 8 bits wide
  Comparator comparator_1 (.a(Reg_ALU_A), .b(Reg_ALU_B), .gt(AgroesserB), .eq(AgleichB), .lt(AkleinerB));
  and and_2 (and_2_out, ~CU_ALU_OPWahl[3], ~CU_ALU_OPWahl[2], ~CU_ALU_OPWahl[1], CU_ALU_OPWahl[0], CU_ALU_OP);  // AND_Gate
  and and_3 (and_3_out, ~CU_ALU_OPWahl[3], ~CU_ALU_OPWahl[2], ~CU_ALU_OPWahl[1], ~CU_ALU_OPWahl[0], CU_ALU_OP);  // AND_Gate
  and and_4 (and_4_out, adder_1_cout, and_3_out);
  and and_5 (Negativ, and_7_out, subtractor_2_bout);
  and and_6 (Carry, and_4_out, adder_2_cout);
  and and_7 (and_7_out, subtractor_1_bout, and_2_out);
  Multiplexer #(.select(4), .width(8)) multiplexer_1 (
    .in0(adder_1_out), .in1(subtractor_1_out), .in2(adder_2_out), .in3(subtractor_2_out),
    .in4(multiplier_1_out), .in5(multiplier_1_cout), .in6(divider_1_out), .in7(divider_1_rem),
    .in8(not_1_out), .in9(and_1_out), .in10(or_1_out), .in11(xor_1_out), .in12(negator_1_out),
    .in13(xnor_1_out), .in14(nor_1_out), .in15(nand_1_out), .out(ALU_Reg_C), .sel(CU_ALU_OPWahl),
    .en(CU_ALU_OP));
endmodule

module GPU_Register (
  input  [7:0] CU_Reg_Adresse,
  input  [7:0] ALU_Reg_C,
  input  [7:0] CU_Reg_Wert,
  input  [7:0] RAM_Reg_Wert,
  input  [7:0] CU_Reg_Steuerung,
  input  Carry,
  input  Negativ,
  input  AgroesserB,
  input  AgleichB,
  input  AkleinerB,
  input  Takt,
  output [7:0] Reg_RAM_Daten,
  output [7:0] Reg_ALU_A,
  output [15:0] Reg_Out_Adr,
  output [7:0] Reg_ALU_B,
  output [7:0] Reg_Out_Daten,
  output [7:0] Reg_CU_Status
);

  wire [7:0] bit_extender_1_out, multiplexer_1_out, ram_1_dout;

  assign bit_extender_1_out = {{3{1'b0}}, {AkleinerB, AgleichB, AgroesserB, Negativ, Carry}};  // Bit_Extender bit_extender_1
  Multiplexer #(.select(2), .width(8), .enable("false")) multiplexer_1 (
    .in0(Reg_ALU_A), .in1(ALU_Reg_C), .in2(CU_Reg_Wert), .in3(RAM_Reg_Wert), .out(multiplexer_1_out),
    .sel(CU_Reg_Steuerung[1:0]));
  RAM #(.trigger("falling"), .databus("bibus")) ram_1 (
    .addr(CU_Reg_Adresse), .we(CU_Reg_Steuerung[2]), .oe(CU_Reg_Steuerung[3]), .clk(Takt),
    .din(multiplexer_1_out), .dout(ram_1_dout));
  Register Status (
    .D(bit_extender_1_out), .en(CU_Reg_Steuerung[6]), .clk(Takt), .Q(Reg_CU_Status), .clr(CU_Reg_Steuerung[7]));
  Register BufferA (.D(ram_1_dout), .en(CU_Reg_Steuerung[4]), .clk(Takt), .Q(Reg_ALU_A), .clr(CU_Reg_Steuerung[7]));
  Register BufferB (.D(ram_1_dout), .en(CU_Reg_Steuerung[5]), .clk(Takt), .Q(Reg_ALU_B), .clr(CU_Reg_Steuerung[7]));

  assign Reg_Out_Adr = {Reg_ALU_B, Reg_ALU_A};
  assign Reg_Out_Daten = Reg_ALU_B;
  assign Reg_RAM_Daten = Reg_ALU_A;
endmodule

module Mod4_Speicher (
  input  [7:0] CPU_Mod4_Adresse,
  input  CPU_Mod4_Weiter,
  input  CPU_Mod4_WeiterZwei,
  input  [15:0] CPU_Mod4_Daten,
  input  CPU_Mod4_Sende,
  input  Mod_Mod4_Daisychain,
  input  CPU_Mod4_IntMaskiert,
  input  Takt,
  input  [15:0] RAM_Mod4_Daten,
  output Mod4_Out_SvWert,
  output [15:0] Mod4_Out_Wert,
  output [7:0] Mod4_Out_ICNummer,
  output Mod4_Out_Daisychain,
  output [23:0] Mod4_RAM_Adr,
  output [15:0] Mod4_RAM_Daten,
  output Mod4_RAM_Speicher,
  output Mod4_RAM_Lade
);

  wire and_1_out, and_2_out, and_3_out, and_4_out, and_6_out, and_7_out, comparator_1_eq, d_ff_1_q,
       decoder_1_out1, decoder_2_out0, decoder_2_out1, decoder_2_out2, decoder_2_out3, decoder_2_out4,
       not_1_out, or_1_out, or_2_out, or_4_out, or_5_out, or_6_out, register_2_q, t_ff_1_q;
  wire [7:0] multiplexer_1_out, multiplexer_2_out;
  wire [15:0] register_1_q;

  Comparator #(.mode("unsigned")) comparator_1 (.a(8'h4), .b(CPU_Mod4_Adresse), .eq(comparator_1_eq));  // open: gt, lt
  Register #(.width(16), .trigger("falling")) register_1 (
    .D(CPU_Mod4_Daten), .en(and_2_out), .clk(Takt), .Q(register_1_q), .clr(and_3_out));
  or or_1 (or_1_out, and_2_out, t_ff_1_q);
  T_Flip_Flop #(.trigger("falling")) t_ff_1 (.T(or_1_out), .clk(Takt), .Q(t_ff_1_q));  // open: Qn, reset, preset
  and and_1 (and_1_out, comparator_1_eq, CPU_Mod4_Sende);
  and and_2 (and_2_out, and_1_out, CPU_Mod4_WeiterZwei);
  and and_3 (and_3_out, ~and_2_out, ~t_ff_1_q);  // AND_Gate
  D_Flip_Flop d_ff_1 (.Q(d_ff_1_q), .preset(Mod4_Out_SvWert), .reset(not_1_out));  // open: D, clk, Qn
  not not_1 (not_1_out, and_4_out);
  and and_4 (and_4_out, CPU_Mod4_IntMaskiert, ~Mod_Mod4_Daisychain);  // AND_Gate
  and and_5 (Mod4_Out_SvWert, ~Mod_Mod4_Daisychain, CPU_Mod4_WeiterZwei, and_6_out);  // AND_Gate
  Decoder #(.select(4), .enable("false")) decoder_1 (
    .out1(decoder_1_out1), .out2(Mod4_RAM_Speicher), .out3(Mod4_RAM_Lade), .sel(register_1_q[15:12]));  // open: out0, out4, out5, out6, out7, out8, out9, out10, out11, out12, out13, out14, out15
  or or_2 (or_2_out, Mod4_Out_SvWert, d_ff_1_q);
  assign Mod4_Out_ICNummer = or_2_out ? 8'h4 : 8'bz;  // Controlled_Buffer controlled_buffer_1
  Pull_Resistor pull_resistor_1 (.node(Mod4_Out_ICNummer));
  or or_3 (Mod4_Out_Daisychain, Mod_Mod4_Daisychain, d_ff_1_q);
  and and_6 (and_6_out, CPU_Mod4_IntMaskiert, register_2_q, CPU_Mod4_WeiterZwei);
  and and_7 (and_7_out, ~or_2_out, d_ff_1_q, CPU_Mod4_IntMaskiert);  // AND_Gate
  or or_4 (or_4_out, Mod4_RAM_Lade, and_7_out);
  Decoder #(.select(4)) decoder_2 (
    .out0(decoder_2_out0), .out1(decoder_2_out1), .out2(decoder_2_out2), .out3(decoder_2_out3),
    .out4(decoder_2_out4), .sel(register_1_q[11:8]), .en(decoder_1_out1));  // open: out5, out6, out7, out8, out9, out10, out11, out12, out13, out14, out15
  Register #(.width(1), .trigger("falling")) register_2 (
    .D(Mod4_RAM_Lade), .en(or_4_out), .clk(Takt), .Q(register_2_q));  // open: clr
  or or_5 (or_5_out, Mod4_RAM_Lade, decoder_2_out3);
  or or_6 (or_6_out, Mod4_RAM_Lade, decoder_2_out4);
  Register #(.trigger("falling")) AdrL (
    .D(register_1_q[7:0]), .en(decoder_2_out0), .clk(Takt), .Q(Mod4_RAM_Adr[7:0]));  // open: clr
  Register #(.trigger("falling")) AdrM (
    .D(register_1_q[7:0]), .en(decoder_2_out1), .clk(Takt), .Q(Mod4_RAM_Adr[15:8]));  // open: clr
  Register #(.trigger("falling")) AdrH (
    .D(register_1_q[7:0]), .en(decoder_2_out2), .clk(Takt), .Q(Mod4_RAM_Adr[23:16]));  // open: clr
  Register #(.trigger("falling")) DatenL (
    .D(multiplexer_1_out), .en(or_5_out), .clk(Takt), .Q(Mod4_RAM_Daten[7:0]));  // open: clr
  Multiplexer #(.width(8), .enable("false")) multiplexer_1 (
    .in0(register_1_q[7:0]), .in1(RAM_Mod4_Daten[7:0]), .out(multiplexer_1_out), .sel(Mod4_RAM_Lade));
  Register #(.trigger("falling")) DatenH (
    .D(multiplexer_2_out), .en(or_6_out), .clk(Takt), .Q(Mod4_RAM_Daten[15:8]));  // open: clr
  Multiplexer #(.width(8), .enable("false")) multiplexer_2 (
    .in0(register_1_q[7:0]), .in1(RAM_Mod4_Daten[15:8]), .out(multiplexer_2_out), .sel(Mod4_RAM_Lade));
  Pull_Resistor pull_resistor_2 (.node(Mod4_Out_Wert));
  assign Mod4_Out_Wert = Mod4_Out_SvWert ? Mod4_RAM_Daten : 16'bz;  // Controlled_Buffer controlled_buffer_2
endmodule
